# Fritzing sketch Carro-Herbart-SONAR (saved by Fritzing 0.8.7b)

parts:
  J1 = Basic Servo
  M1 = DC Motor
  S2 = H-Bridge with L298N
  Componente1 = Freaduino 1.8
  VCC4 = Battery
  VCC5 = Battery
  S3 = SPST Switch [package=switch-spdt-smd]
  VCC1 = Battery block 9V
  U1 = Bluetooth HC-05 Fêmea [part_number=3459898989898]

nets:
  N1: J1.gnd, Componente1.FD9-
  N2: J1.vcc, Componente1.FD9+
  N3: J1.pulse, Componente1.FD9
  N4: M1.pin_1, S2.OUT1-Motor1
  N5: M1.pin_2, S2.OUT2-Motor1
  N6: S2.12V, VCC4.+
  N7: S2.IN1, Componente1.FD11
  N8: S2.IN2, Componente1.FD12
  N9: Componente1.FD1, U1.RXD
  N10: Componente1.FD13-, VCC5.-
  N11: Componente1.FD0, U1.TXD
  N12: Componente1.FD0+, U1.VCC
  N13: Componente1.FD0-, U1.GND
  N14: S3.S, VCC1.+

notes:
  Micro Servo SG90

custom parts:
  H-Bridge with L298N: h-bridge
  Freaduino 1.8: Freaduino UNO is an Arduino compatible board. It is based on Arduino UNO Rev3 design. So you can use Freaduino as Arduino UNO Rev3 . All code, shield and IDE for Arduino UNO Rev3 are also valid on Freaduino UNO. Some visible improvement on hardware make Freaduino UNO more flexible and easier to use. For example: 3.3v or 5v IO selectable allow you connect some 3.3v modules (such as XBee) to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
  Bluetooth HC-05 Fêmea: Bluetooth module uses HC-05
