# Fritzing sketch CnE-Boneco1-arduino-nano-protoboard400 (saved by Fritzing 0.9.2b)
breadboards: 1

parts:
  Componente1 = Arduino Nano (Rev3.0) (ICSP)
  LED3 = LED - 5mm [color="Green (565nm)" package="5 mm [THT]"]
  LED4 = LED - 5mm [color="Green (565nm)" package="5 mm [THT]"]
  J1 = Basic Servo
  Componente2 = SRF05 Ultrasonic Rangefinder

nets:
  GND: Componente1.GND, LED3.cathode, LED4.cathode, J1.gnd, Componente2.GND
  N1: Componente1.D6, Componente2.Trig, Componente2.Echo
  N2: Componente1.D9, J1.pulse
  N3: Componente1.D10, LED3.anode, LED4.anode
  VCC: Componente1.5V, J1.vcc, Componente2.VCC
