# Fritzing sketch ConfiguraModuloBluetooth (saved by Fritzing 0.8.7b)
breadboards: 1

parts:
  Componente1 = Bluetooth HC-05 Macho
  Componente2 = Arduino Uno (Rev3)

nets:
  N1: Componente1.TXD, Componente2.D10_PWM/SS
  N2: Componente1.RXD, Componente2.D11_PWM/MOSI
  VCC: Componente1.VCC, Componente2.5V
  N3: Componente1.Key, Componente2.D9_PWM
  GND: Componente1.GND, Componente2.GND
