# Fritzing sketch Talking-Tom (saved by Fritzing 0.8.7b)
breadboards: 1

parts:
  Componente1 = Arduino Uno (Rev3)
  J1 = Infrared Proximity Sensor
  J2 = Basic Servo
  J3 = Basic Servo
  LED2 = LED - 5mm [color="Green (565nm)" package="5 mm [THT]"]
  LED3 = LED - 5mm [color="Green (565nm)" package="5 mm [THT]"]

nets:
  N1: Componente1.D10_PWM/SS, J3.pulse
  N2: Componente1.D11_PWM/MOSI, J2.pulse
  N3: Componente1.D6_PWM, J1.Vout
  N4: Componente1.D7, LED2.anode, LED3.anode
  VCC: Componente1.5V, J1.Vcc, J2.vcc, J3.vcc
  GND: Componente1.GND, J1.GND, J2.gnd, J3.gnd, LED2.cathode, LED3.cathode
