# Fritzing sketch inseto (saved by Fritzing 0.8.7b)

parts:
  Componente1 = Freaduino 1.8
  J1 = Basic Servo
  J2 = Basic Servo
  VCC1 = Battery block 9V  # not connected
  S1 = SPST Switch [package=switch-spdt-smd]  # not connected

nets:
  N1: Componente1.FD9, J2.pulse
  N2: Componente1.FD9+, J2.vcc
  N3: Componente1.FD9-, J2.gnd
  N4: Componente1.FD10, J1.pulse
  N5: Componente1.FD10+, J1.vcc
  N6: Componente1.FD10-, J1.gnd

custom parts:
  Freaduino 1.8: Freaduino UNO is an Arduino compatible board. It is based on Arduino UNO Rev3 design. So you can use Freaduino as Arduino UNO Rev3 . All code, shield and IDE for Arduino UNO Rev3 are also valid on Freaduino UNO. Some visible improvement on hardware make Freaduino UNO more flexible and easier to use. For example: 3.3v or 5v IO selectable allow you connect some 3.3v modules (such as XBee) to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
